// Logisim project mesm_6.circ as structural Verilog: 6 circuits, main circuit main
module main (
);

  CU ControlUnit ();  // open: cmd, sel_acc, sel_md, sel_mw, w_m, sel_mr, m_use, sel_pc, sel_addr, sel_j_addr, w_a, w_c, w_y, a_neg, a_zero, clear_c, enter_int, exit_int, w_pc
  PC_reg pc_reg_1 ();  // open: clk, w_pc, U_addr, V_addr, M_i, imm, pc_q
endmodule

module CU (
  input  [23:0] cmd,
  output [2:0] sel_acc,
  output [2:0] sel_md,
  output [1:0] sel_mw,
  output w_m,
  output [1:0] sel_mr,
  output m_use,
  output [2:0] sel_pc,
  output sel_addr,
  output sel_j_addr,
  output w_a,
  output w_c,
  output w_y,
  output a_neg,
  output a_zero,
  output clear_c,
  output enter_int,
  output exit_int,
  output w_pc
);

  wire alu_done, and_1_out, and_2_out, and_3_out, and_4_out, branch, busy, clk, comparator_1_eq,
       comparator_2_eq, comparator_3_eq, dbus_done, dbus_read, dbus_write, decode, fetch, ibus_done, irq,
       not_1_out, not_2_out, not_3_out, not_4_out, not_5_out, op_not_cached, or_1_out, or_3_out, reset,
       sel_c_mem;
  wire [5:0] alu_op;
  wire [8:0] adder_1_out, imm, L_data, multiplexer_1_out, multiplexer_2_out, multiplexer_3_out,
       multiplexer_6_out, multiplexer_7_out, multiplexer_8_out, S_data, upc_q;
  wire [14:0] dbus_addr, ibus_addr;
  wire [23:0] D_RAM_H_dout, D_RAM_L_dout, dbus_idata_h, dbus_idata_l, dbus_odata_h, dbus_odata_l,
       I_ROM_H_data, I_ROM_L_data, ibus_data_h, ibus_data_l, multiplexer_4_out, multiplexer_5_out;
  wire [31:3] uop_h;

  Clock u_CLK (.out(clk));
  Button u_RESET ();  // open: out
  Button u_IRQ (.out(irq));
  Pull_Resistor #(.pull(1)) pull_resistor_1 (.node(reset));
  not not_1 (not_1_out, alu_done);
  or or_1 (or_1_out, dbus_read, dbus_write);
  not not_2 (not_2_out, dbus_done);
  not not_3 (not_3_out, ibus_done);
  Comparator #(.width(6)) comparator_1 (.a(alu_op), .b({6{1'b0}}), .eq(comparator_1_eq));  // open: gt, lt
  not not_4 (not_4_out, comparator_1_eq);
  and and_1 (and_1_out, or_1_out, not_2_out);
  and and_2 (and_2_out, fetch, not_3_out);
  and and_3 (and_3_out, not_4_out, not_1_out);
  ROM #(.addrWidth(15), .dataWidth(24)) I_ROM_L (.addr(ibus_addr), .data(I_ROM_L_data));
  ROM #(.addrWidth(6), .dataWidth(9)) S (.addr(cmd[17:12]), .data(S_data));
  ROM #(.addrWidth(4), .dataWidth(9)) L (.addr(cmd[18:15]), .data(L_data));
  or or_2 (busy, and_1_out, and_2_out, and_3_out);
  RAM #(.addrWidth(15), .dataWidth(24), .databus("bibus")) D_RAM_L (
    .addr(dbus_addr), .we(dbus_write), .oe(dbus_read), .clk(clk), .din(dbus_idata_l), .dout(D_RAM_L_dout));
  RAM #(.addrWidth(15), .dataWidth(24), .databus("bibus")) D_RAM_H (
    .addr(dbus_addr), .we(dbus_write), .oe(dbus_read), .clk(clk), .din(dbus_idata_h), .dout(D_RAM_H_dout));
  Register #(.width(24)) u_IBUS_DATA_L (.D(I_ROM_L_data), .en(and_4_out), .clk(clk), .Q(ibus_data_l), .clr(1'b0));
  Multiplexer #(.width(9), .enable("false")) multiplexer_1 (
    .in0(S_data), .in1(L_data), .out(multiplexer_1_out), .sel(cmd[19]));
  ROM #(.addrWidth(15), .dataWidth(24)) I_ROM_H (.addr(ibus_addr), .data(I_ROM_H_data));
  Multiplexer #(.width(9), .enable("false")) multiplexer_2 (
    .in0(multiplexer_1_out), .in1(9'h7), .out(multiplexer_2_out), .sel(irq));
  and and_4 (and_4_out, fetch, not_5_out);
  Register #(.width(1)) u_ibus_done (.D(fetch), .en(1'b1), .clk(clk), .Q(ibus_done), .clr(1'b0));
  Adder #(.width(9)) adder_1 (.a(9'h1), .b(upc_q), .out(adder_1_out));  // open: cin, cout
  Comparator #(.width(15)) comparator_2 (.a(dbus_addr), .b({15{1'b0}}), .eq(comparator_2_eq));  // open: gt, lt
  Comparator #(.width(15)) comparator_3 (.a(dbus_addr), .b({15{1'b0}}), .eq(comparator_3_eq));  // open: gt, lt
  Multiplexer #(.width(9), .enable("false")) multiplexer_3 (
    .in0(adder_1_out), .in1(multiplexer_2_out), .out(multiplexer_3_out), .sel(decode));
  ROM #(.addrWidth(9), .dataWidth(32)) MC_L (
    .addr(multiplexer_8_out),
    .data({sel_j_addr, sel_addr, sel_pc, m_use, sel_mr, w_m, sel_mw, sel_md, sel_acc, alu_op, imm}));
  not not_5 (not_5_out, ibus_done);
  Multiplexer #(.width(24), .enable("false")) multiplexer_4 (
    .in0(D_RAM_L_dout), .in1({24{1'b0}}), .out(multiplexer_4_out), .sel(comparator_2_eq));
  Multiplexer #(.width(24), .enable("false")) multiplexer_5 (
    .in0(D_RAM_H_dout), .in1({24{1'b0}}), .out(multiplexer_5_out), .sel(comparator_3_eq));
  Multiplexer #(.width(9), .enable("false")) multiplexer_6 (
    .in0(multiplexer_3_out), .in1(imm), .out(multiplexer_6_out), .sel(branch));
  Register #(.width(24)) u_IBUS_DATA_H (.D(I_ROM_H_data), .en(and_4_out), .clk(clk), .Q(ibus_data_h), .clr(1'b0));
  Register #(.width(24)) u_DBUS_ODATA_L (
    .D(multiplexer_4_out), .en(dbus_read), .clk(clk), .Q(dbus_odata_l), .clr(1'b0));
  Register #(.width(1)) u_DBUS_DONE (.D(or_3_out), .en(1'b1), .clk(clk), .Q(dbus_done), .clr(1'b0));
  or or_3 (or_3_out, dbus_write, dbus_read);
  Register #(.width(24)) u_DBUS_ODATA_H (
    .D(multiplexer_5_out), .en(dbus_read), .clk(clk), .Q(dbus_odata_h), .clr(1'b0));
  Multiplexer #(.width(9), .enable("false")) multiplexer_7 (
    .in0(multiplexer_6_out), .in1(upc_q), .out(multiplexer_7_out), .sel(busy));
  Multiplexer #(.width(9), .enable("false")) multiplexer_8 (
    .in0(multiplexer_7_out), .in1({9{1'b0}}), .out(multiplexer_8_out), .sel(reset));
  // Probe on {sel_j_addr, sel_addr, sel_pc, m_use, sel_mr, w_m, sel_mw, sel_md, sel_acc, alu_op, imm}
  Register #(.width(9)) upc (.D(multiplexer_8_out), .en(1'b1), .clk(clk), .Q(upc_q), .clr(1'b0));
  ROM #(.addrWidth(9), .dataWidth(32)) MC_H (
    .addr(multiplexer_8_out),
    .data({uop_h[31:17], w_pc, exit_int, enter_int, clear_c, branch, a_zero, a_neg, w_y, w_c, w_a, dbus_write, dbus_read, decode, uop_h[3], fetch, op_not_cached, sel_c_mem}));
  // Probe on upc_q

  // Other names for the same wires on the sheet: uop_h (some bits) = {w_pc, exit_int, enter_int, clear_c, branch, a_zero, a_neg, w_y, w_c, w_a, dbus_write, dbus_read, decode, fetch, op_not_cached, sel_c_mem};
  //   ibus_fetch = fetch; w_opcode = uop_h[3]; mem_r = dbus_read; mem_w = dbus_write;
  //   uop_l[31:0] = {sel_j_addr, sel_addr, sel_pc, m_use, sel_mr, w_m, sel_mw, sel_md, sel_acc, alu_op, imm}

  // Notes on the sheet:
  //   contents of S (hex, n*v repeats v):
  //   19 1b 1c 1d 1e 1f 20 21 22 24 27 2a 2d 2e 31 32 33 34 35 36 37 38 39 3a 3b 3c 3d 3e 3f 40 41 42 43
  //   45 46 48 49 4a 4b 4c 4d 4e 4f 50 51 52 53 54 55 56 57 58 59 5a 5b 5c 5d 5e 5f 60 61 62 63 64
  //   contents of L (hex, n*v repeats v):
  //   65 66 67 69 6b 6c 6d 71 75 77 79 7a 7b 7f 83 84
  //   contents of MC_L (hex, n*v repeats v):
  //   a40000 1010000 a40001 a40002 a40003 a40004 a40005 a40006 a40007 a40008 a40009 a4000a a4000b a4000c
  //   a4000d a4000e a4000f 18000001 4*0 12 0 12 0 8*12 8000 12 8000 200 12 8000 600 12 8000 a00 12 12 8000
  //   400 19*12 e40012 12 12 3010000 12 12 c80012 82d80012 28*12 0 14 0 14 940012 980012 6f 12 0 12 73 12
  //   0 12 0 12 8800000 12 12 12 7d 12 8000000 12 4000081 12 8000000 12 12 4000086 12 88c0000 12
  //   contents of MC_H (hex, n*v repeats v):
  //   0 80 15*0 18000 c 10 c 2010 12 4000 12 40 8*12 a0 12 20 40080 12 20 40080 12 20 40080 12 12 20 40080
  //   22*12 80 32*12 100 2012 121 2012 12 12 800 12 10000 12 200 12 10000 12 10000 12 10000 12 12 12 20000
  //   12 10000 12 0 12 10000 12 12 0 12 10000 12
endmodule

module PC_reg (
  input  clk,
  input  w_pc,
  input  [15:0] U_addr,
  input  [15:0] V_addr,
  input  [15:0] M_i,
  input  [15:0] imm,
  output [15:0] pc_q
);

  wire [15:0] adder_1_out, multiplexer_1_out;

  // Probe on adder_1_out
  Multiplexer #(.select(3), .width(16), .enable("false")) multiplexer_1 (
    .in0(U_addr), .in1(V_addr), .in2(M_i), .in3(imm), .in4(adder_1_out), .out(multiplexer_1_out));  // open: in5, in6, in7, sel
  Register #(.width(16)) PC (.D(multiplexer_1_out), .en(w_pc), .clk(clk), .Q(pc_q), .clr(1'b0));
  Adder #(.width(16)) adder_1 (.a(pc_q), .b(16'h1), .out(adder_1_out));  // open: cin, cout
endmodule

module C_reg (
  input  sel_c,
  input  [14:0] U_addr,
  input  [14:0] dbus_out,
  input  w_c,
  input  clk,
  output [14:0] C_q
);

  wire [14:0] multiplexer_1_out;

  Multiplexer #(.width(15), .enable("false")) multiplexer_1 (
    .in0(U_addr), .in1(dbus_out), .out(multiplexer_1_out), .sel(sel_c));
  Register #(.width(15)) C_reg (.D(multiplexer_1_out), .en(w_c), .clk(clk), .Q(C_q), .clr(1'b0));
endmodule

module U_addr_gen (
  input  clk,
  input  sel_j_add,
  input  c_active,
  input  [23:0] cmd,
  input  [14:0] C_in,
  input  decode,
  input  [14:0] M_j,
  input  [14:0] M_i,
  output [14:0] U_addr
);

  wire [14:0] adder_1_out, bit_extender_1_out, multiplexer_1_out, multiplexer_2_out, multiplexer_3_out,
       V_ADDR_q;

  assign bit_extender_1_out = {{2{cmd[18]}}, {cmd[18], cmd[11:0]}};  // Bit_Extender bit_extender_1
  Multiplexer #(.width(15), .enable("false")) multiplexer_1 (
    .in0(bit_extender_1_out), .in1(cmd[14:0]), .out(multiplexer_1_out), .sel(cmd[19]));
  Adder #(.width(15)) adder_1 (.a(multiplexer_1_out), .b(C_in), .out(adder_1_out));  // open: cin, cout
  Multiplexer #(.width(15), .enable("false")) multiplexer_2 (
    .in0(multiplexer_1_out), .in1(adder_1_out), .out(multiplexer_2_out), .sel(c_active));
  Register #(.width(15)) V_ADDR (.D(multiplexer_2_out), .en(decode), .clk(clk), .Q(V_ADDR_q), .clr(1'b0));
  Multiplexer #(.width(15), .enable("false")) multiplexer_3 (
    .in0(V_ADDR_q), .in1(M_j), .out(multiplexer_3_out), .sel(sel_j_add));
  Adder #(.width(15)) adder_2 (.a(multiplexer_3_out), .b(M_i), .out(U_addr));  // open: cin, cout

  // Notes on the sheet:
  //   op_addr
  //   C + op_addr
endmodule

module M_regs (
  input  clk,
  input  [1:0] sel_mr,
  input  [3:0] reg_ind,
  input  [3:0] imm,
  input  [14:0] V_addr,
  input  [14:0] U_addr,
  input  [1:0] sel_mw,
  input  w_m,
  input  [2:0] sel_md,
  input  [14:0] PC,
  input  [14:0] ACC,
  input  [14:0] M_i,
  input  [14:0] M_i_p1,
  input  [14:0] M_i_m1,
  output [14:0] RD1,
  output [14:0] RD2
);

  wire decoder_1_out1, decoder_1_out2, decoder_1_out3, decoder_1_out4, decoder_1_out5, decoder_1_out6,
       decoder_1_out7, decoder_1_out8, decoder_1_out9, decoder_1_out10, decoder_1_out11, decoder_1_out12,
       decoder_1_out13, decoder_1_out14, decoder_1_out15, decoder_2_out1, decoder_2_out2, decoder_2_out3,
       decoder_2_out4, decoder_2_out5, decoder_2_out6, decoder_2_out7, decoder_2_out8, decoder_2_out9,
       decoder_2_out10, decoder_2_out11, decoder_2_out12, decoder_2_out13, decoder_2_out14, decoder_2_out15,
       decoder_3_out1, decoder_3_out2, decoder_3_out3, decoder_3_out4, decoder_3_out5, decoder_3_out6,
       decoder_3_out7, decoder_3_out8, decoder_3_out9, decoder_3_out10, decoder_3_out11, decoder_3_out12,
       decoder_3_out13, decoder_3_out14, decoder_3_out15;
  wire [3:0] bit_extender_1_out, bit_extender_2_out, multiplexer_1_out, multiplexer_2_out;
  wire [14:0] M1_q, M2_q, M3_q, M4_q, M5_q, M6_q, M7_q, M8_q, M9_q, M10_q, M11_q, M12_q, M13_q, M14_q, M15_q,
       multiplexer_3_out;

  Bit_Extender #(.in_width(15), .out_width(4), .\type ("zero")) bit_extender_1 (.in(V_addr), .out(bit_extender_1_out));
  Bit_Extender #(.in_width(15), .out_width(4), .\type ("zero")) bit_extender_2 (.in(U_addr), .out(bit_extender_2_out));
  Multiplexer #(.select(2), .width(4)) multiplexer_1 (
    .in0(reg_ind), .in1(imm), .in2(bit_extender_1_out), .in3(bit_extender_2_out), .out(multiplexer_1_out),
    .sel(sel_mw), .en(w_m));
  Multiplexer #(.select(2), .width(4), .enable("false")) multiplexer_2 (
    .in0(reg_ind), .in1(imm), .in2(bit_extender_1_out), .in3(bit_extender_2_out), .out(multiplexer_2_out),
    .sel(sel_mr));
  Multiplexer #(.select(3), .width(15), .enable("false")) multiplexer_3 (
    .in0(PC), .in1(ACC), .in2(M_i), .in3(M_i_p1), .in4(M_i_m1), .in5(V_addr), .in6(U_addr),
    .out(multiplexer_3_out), .sel(sel_md));  // open: in7
  Decoder #(.select(4), .enable("false")) decoder_1 (
    .out1(decoder_1_out1), .out2(decoder_1_out2), .out3(decoder_1_out3), .out4(decoder_1_out4),
    .out5(decoder_1_out5), .out6(decoder_1_out6), .out7(decoder_1_out7), .out8(decoder_1_out8),
    .out9(decoder_1_out9), .out10(decoder_1_out10), .out11(decoder_1_out11), .out12(decoder_1_out12),
    .out13(decoder_1_out13), .out14(decoder_1_out14), .out15(decoder_1_out15), .sel(multiplexer_1_out));  // open: out0
  Register #(.width(15)) M1 (.D(multiplexer_3_out), .en(decoder_1_out1), .clk(clk), .Q(M1_q), .clr(1'b0));
  Register #(.width(15)) M2 (.D(multiplexer_3_out), .en(decoder_1_out2), .clk(clk), .Q(M2_q), .clr(1'b0));
  Register #(.width(15)) M3 (.D(multiplexer_3_out), .en(decoder_1_out3), .clk(clk), .Q(M3_q), .clr(1'b0));
  Register #(.width(15)) M4 (.D(multiplexer_3_out), .en(decoder_1_out4), .clk(clk), .Q(M4_q), .clr(1'b0));
  assign RD1 = decoder_2_out1 ? M1_q : 15'bz;  // Controlled_Buffer controlled_buffer_1
  assign RD2 = decoder_3_out1 ? M1_q : 15'bz;  // Controlled_Buffer controlled_buffer_2
  Decoder #(.select(4), .enable("false")) decoder_2 (
    .out1(decoder_2_out1), .out2(decoder_2_out2), .out3(decoder_2_out3), .out4(decoder_2_out4),
    .out5(decoder_2_out5), .out6(decoder_2_out6), .out7(decoder_2_out7), .out8(decoder_2_out8),
    .out9(decoder_2_out9), .out10(decoder_2_out10), .out11(decoder_2_out11), .out12(decoder_2_out12),
    .out13(decoder_2_out13), .out14(decoder_2_out14), .out15(decoder_2_out15), .sel(multiplexer_2_out));  // open: out0
  assign RD1 = decoder_2_out2 ? M2_q : 15'bz;  // Controlled_Buffer controlled_buffer_3
  assign RD2 = decoder_3_out2 ? M2_q : 15'bz;  // Controlled_Buffer controlled_buffer_4
  assign RD1 = decoder_2_out3 ? M3_q : 15'bz;  // Controlled_Buffer controlled_buffer_5
  assign RD2 = decoder_3_out3 ? M3_q : 15'bz;  // Controlled_Buffer controlled_buffer_6
  assign RD1 = decoder_2_out4 ? M4_q : 15'bz;  // Controlled_Buffer controlled_buffer_7
  assign RD2 = decoder_3_out4 ? M4_q : 15'bz;  // Controlled_Buffer controlled_buffer_8
  Decoder #(.select(4), .enable("false")) decoder_3 (
    .out1(decoder_3_out1), .out2(decoder_3_out2), .out3(decoder_3_out3), .out4(decoder_3_out4),
    .out5(decoder_3_out5), .out6(decoder_3_out6), .out7(decoder_3_out7), .out8(decoder_3_out8),
    .out9(decoder_3_out9), .out10(decoder_3_out10), .out11(decoder_3_out11), .out12(decoder_3_out12),
    .out13(decoder_3_out13), .out14(decoder_3_out14), .out15(decoder_3_out15), .sel(bit_extender_1_out));  // open: out0
  Register #(.width(15)) M5 (.D(multiplexer_3_out), .en(decoder_1_out5), .clk(clk), .Q(M5_q), .clr(1'b0));
  Register #(.width(15)) M6 (.D(multiplexer_3_out), .en(decoder_1_out6), .clk(clk), .Q(M6_q), .clr(1'b0));
  Register #(.width(15)) M7 (.D(multiplexer_3_out), .en(decoder_1_out7), .clk(clk), .Q(M7_q), .clr(1'b0));
  Register #(.width(15)) M8 (.D(multiplexer_3_out), .en(decoder_1_out8), .clk(clk), .Q(M8_q), .clr(1'b0));
  assign RD1 = decoder_2_out5 ? M5_q : 15'bz;  // Controlled_Buffer controlled_buffer_9
  assign RD2 = decoder_3_out5 ? M5_q : 15'bz;  // Controlled_Buffer controlled_buffer_10
  assign RD1 = decoder_2_out6 ? M6_q : 15'bz;  // Controlled_Buffer controlled_buffer_11
  assign RD2 = decoder_3_out6 ? M6_q : 15'bz;  // Controlled_Buffer controlled_buffer_12
  assign RD1 = decoder_2_out7 ? M7_q : 15'bz;  // Controlled_Buffer controlled_buffer_13
  assign RD2 = decoder_3_out7 ? M7_q : 15'bz;  // Controlled_Buffer controlled_buffer_14
  assign RD1 = decoder_2_out8 ? M8_q : 15'bz;  // Controlled_Buffer controlled_buffer_15
  assign RD2 = decoder_3_out8 ? M8_q : 15'bz;  // Controlled_Buffer controlled_buffer_16
  Register #(.width(15)) M9 (.D(multiplexer_3_out), .en(decoder_1_out9), .clk(clk), .Q(M9_q), .clr(1'b0));
  Register #(.width(15)) M10 (.D(multiplexer_3_out), .en(decoder_1_out10), .clk(clk), .Q(M10_q), .clr(1'b0));
  Register #(.width(15)) M11 (.D(multiplexer_3_out), .en(decoder_1_out11), .clk(clk), .Q(M11_q), .clr(1'b0));
  Register #(.width(15)) M12 (.D(multiplexer_3_out), .en(decoder_1_out12), .clk(clk), .Q(M12_q), .clr(1'b0));
  assign RD1 = decoder_2_out9 ? M9_q : 15'bz;  // Controlled_Buffer controlled_buffer_17
  assign RD2 = decoder_3_out9 ? M9_q : 15'bz;  // Controlled_Buffer controlled_buffer_18
  assign RD1 = decoder_2_out10 ? M10_q : 15'bz;  // Controlled_Buffer controlled_buffer_19
  assign RD2 = decoder_3_out10 ? M10_q : 15'bz;  // Controlled_Buffer controlled_buffer_20
  assign RD1 = decoder_2_out11 ? M11_q : 15'bz;  // Controlled_Buffer controlled_buffer_21
  assign RD2 = decoder_3_out11 ? M11_q : 15'bz;  // Controlled_Buffer controlled_buffer_22
  assign RD1 = decoder_2_out12 ? M12_q : 15'bz;  // Controlled_Buffer controlled_buffer_23
  assign RD2 = decoder_3_out12 ? M12_q : 15'bz;  // Controlled_Buffer controlled_buffer_24
  Register #(.width(15)) M13 (.D(multiplexer_3_out), .en(decoder_1_out13), .clk(clk), .Q(M13_q), .clr(1'b0));
  Register #(.width(15)) M14 (.D(multiplexer_3_out), .en(decoder_1_out14), .clk(clk), .Q(M14_q), .clr(1'b0));
  Register #(.width(15)) M15 (.D(multiplexer_3_out), .en(decoder_1_out15), .clk(clk), .Q(M15_q), .clr(1'b0));
  assign RD1 = decoder_2_out13 ? M13_q : 15'bz;  // Controlled_Buffer controlled_buffer_25
  assign RD2 = decoder_3_out13 ? M13_q : 15'bz;  // Controlled_Buffer controlled_buffer_26
  assign RD1 = decoder_2_out14 ? M14_q : 15'bz;  // Controlled_Buffer controlled_buffer_27
  assign RD2 = decoder_3_out14 ? M14_q : 15'bz;  // Controlled_Buffer controlled_buffer_28
  assign RD1 = decoder_2_out15 ? M15_q : 15'bz;  // Controlled_Buffer controlled_buffer_29
  assign RD2 = decoder_3_out15 ? M15_q : 15'bz;  // Controlled_Buffer controlled_buffer_30

  // Notes on the sheet:
  //   RA1
  //   RA2
  //   WA
endmodule
